# Fritzing sketch Wiring diag (saved by Fritzing 0.9.10b)
breadboards: 1

parts:
  U1 = ESP32S-HiLetgo [part_number=ESP32S-HiLetgo]
  RHT1 = Humidity and Temperature Sensor RHT03
  J1 = Basic Servo
  U2 = Sharp PC817 [package=THT]
  R1 = Resistor [tolerance=±5% resistance=5.1k package="2512 [SMD]"]
  C1 = Capacitor [package=cap-pth-small]  # not connected
  R2 = Resistor [tolerance=±5% resistance=1k package="2512 [SMD]"]
  R4 = Resistor [tolerance=±5% resistance=510 package="2512 [SMD]"]
  U3 = TRANSISTOR_NPN_2 [package=to-92]
  U4 = RELAY [package=relay-g5q]
  D1 = P1000K [part_number=P1000K]
  U5 = Sharp PC817 [package=THT]
  R5 = Resistor [tolerance=±5% resistance=1k package="2512 [SMD]"]
  R6 = Resistor [tolerance=±5% resistance=510 package="2512 [SMD]"]
  U6 = RELAY [package=relay-g5q]
  U7 = TRANSISTOR_NPN_2 [package=to-92]
  D2 = P1000K [part_number=P1000K]
  U8 = Sharp PC817 [package=THT]
  R7 = Resistor [tolerance=±5% resistance=1k package="2512 [SMD]"]
  R8 = Resistor [tolerance=±5% resistance=510 package="2512 [SMD]"]
  U9 = RELAY [package=relay-g5q]
  U10 = TRANSISTOR_NPN_2 [package=to-92]
  D3 = P1000K [part_number=P1000K]
  U11 = Sharp PC817 [package=THT]
  R9 = Resistor [tolerance=±5% resistance=1k package="2512 [SMD]"]
  R10 = Resistor [tolerance=±5% resistance=510 package="2512 [SMD]"]
  U12 = RELAY [package=relay-g5q]
  U13 = TRANSISTOR_NPN_2 [package=to-92]
  D4 = P1000K [part_number=P1000K]
  LED1 = LED - 3mm [color="Red (633nm)" current=0.030 package="3 mm [THT]"]
  LED2 = LED - 3mm [color="Red (633nm)" current=0.030 package="3 mm [THT]"]
  LED3 = LED - 3mm [color="Red (633nm)" current=0.030 package="3 mm [THT]"]
  LED4 = LED - 3mm [color="Red (633nm)" current=0.030 package="3 mm [THT]"]

nets:
  N1: U1.3.3, RHT1.Vcc, R2.Pin_1, R5.Pin_1, R7.Pin_1, R9.Pin_1
  GND: U1.GND, RHT1.GND_2, J1.gnd, U3.E
  VIN: U1.VIN, J1.vcc, U2.Pin_4
  N2: U1.GPIO16, J1.pulse
  N3: U1.GPIO17, LED2.cathode
  N4: U1.GPIO18, LED1.cathode
  N5: U1.GPIO19, LED4.cathode
  N6: U1.GPIO23, RHT1.Data-signal, R1.Pin_0
  N7: U2.Pin_1, R2.Pin_0
  N8: U2.Pin_2, LED1.anode
  N9: U2.Pin_3, R4.Pin_0
  N10: R4.Pin_1, U3.B
  N11: U3.C, U4.COIL2, D1.anode
  N12: U4.COIL1, D1.cathode
  N13: U5.Pin_1, R5.Pin_0
  N14: U5.Pin_2, LED2.anode
  N15: U5.Pin_3, R6.Pin_0
  N16: R6.Pin_1, U7.B
  N17: U6.COIL2, U7.C, D2.anode
  N18: U6.COIL1, D2.cathode
  N19: U8.Pin_1, R7.Pin_0
  N20: U8.Pin_2, LED3.anode
  N21: U8.Pin_3, R8.Pin_0
  N22: R8.Pin_1, U10.B
  N23: U9.COIL2, U10.C, D3.anode
  N24: U9.COIL1, D3.cathode
  N25: U11.Pin_1, R9.Pin_0
  N26: U11.Pin_2, LED4.anode
  N27: U11.Pin_3, R10.Pin_0
  N28: R10.Pin_1, U13.B
  N29: U12.COIL2, U13.C, D4.anode
  N30: U12.COIL1, D4.cathode

notes:
  5V rail
  3.3V rail
  DHT22 module
  220VAC Supply
  ALL OUT
  5VDC 3A supply
  IN OUT
  12VDC 150W supply
  IN OUT
  Lighting LEDs 12VDC
  Heater 220VAC
  Fan 220VAC
  Relay module 4 channel

custom parts:
  ESP32S-HiLetgo: HiLetgo ESP-WROOM-32 ESP32 ESP-32S Development Board 2.4GHz Dual-Mode WiFi + Bluetooth Dual Cores Microcontroller The ESP32 integrated with Antenna switches, RF Balun, power amplifiers, low-noise amplifiers, filters, and management modules, and the entire solution occupies the least area of PCB. 2.4 GHz Wi-Fi plus Bluetooth dual-mode chip, with TSMC Ultra-low power consumption 40nm technology,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
